// Logisim project Switch.circ as structural Verilog: 1 circuit, main circuit ThreeCaseSwitch4Bits
module ThreeCaseSwitch4Bits (
  input  [2:0] Value,
  input  [2:0] FirstCase,
  input  [3:0] FirstValue,
  input  [2:0] SecondCase,
  input  [3:0] SecondValue,
  input  [2:0] ThirdCase,
  input  [3:0] ThirdValue,
  input  [3:0] DEFAULT,
  output [3:0] ReturnedValue
);

  wire equality3bits_1_aqab, equality3bits_2_aqab, equality3bits_3_aqab;
  wire [3:0] multiplexer_2_out, multiplexer_3_out;

  Equality3Bits equality3bits_1 (.A(Value), .B(FirstCase), .AQAB(equality3bits_1_aqab));
  Equality3Bits equality3bits_2 (.A(Value), .B(SecondCase), .AQAB(equality3bits_2_aqab));
  Equality3Bits equality3bits_3 (.A(Value), .B(ThirdCase), .AQAB(equality3bits_3_aqab));
  Multiplexer #(.width(4)) multiplexer_1 (
    .in0(multiplexer_2_out), .in1(FirstValue), .out(ReturnedValue), .sel(equality3bits_1_aqab));  // open: en
  Multiplexer #(.width(4)) multiplexer_2 (
    .in0(multiplexer_3_out), .in1(SecondValue), .out(multiplexer_2_out), .sel(equality3bits_2_aqab));  // open: en
  Multiplexer #(.width(4)) multiplexer_3 (
    .in0(DEFAULT), .in1(ThirdValue), .out(multiplexer_3_out), .sel(equality3bits_3_aqab));  // open: en
endmodule
