// Logisim project RC_Controller.circ as structural Verilog: 1 circuit, main circuit RC_Controller
module RC_Controller (
);

  wire D_out, speedsystem_1_a, speedsystem_1_b, speedsystem_1_c, speedsystem_1_d, speedsystem_1_e,
       speedsystem_1_f, speedsystem_1_g, U_out;
  wire [2:0] joystick_1_x, joystick_1_y, joystick_2_x, joystick_2_y;
  wire [3:0] joysticksystem_1_row_0, joysticksystem_1_row_0_2, joysticksystem_1_row_1,
       joysticksystem_1_row_1_2, joysticksystem_1_row_2, joysticksystem_1_row_2_2, joysticksystem_1_row_3,
       joysticksystem_1_row_3_2, joysticksystem_1_row_4, joysticksystem_1_row_4_2, joysticksystem_2_row_0,
       joysticksystem_2_row_0_2, joysticksystem_2_row_1, joysticksystem_2_row_1_2, joysticksystem_2_row_2,
       joysticksystem_2_row_2_2, joysticksystem_2_row_3, joysticksystem_2_row_3_2, joysticksystem_2_row_4,
       joysticksystem_2_row_4_2;

  Joystick #(.bits(3)) joystick_1 (.x(joystick_1_x), .y(joystick_1_y));
  Button U (.out(U_out));
  Button D (.out(D_out));
  Joystick #(.bits(3)) joystick_2 (.x(joystick_2_x), .y(joystick_2_y));
  JoystickSystem joysticksystem_1 (
    .JoystickX(joystick_1_x), .JoystickY(joystick_1_y), .Row_0(joysticksystem_1_row_0),
    .Row_1(joysticksystem_1_row_1), .Row_2(joysticksystem_1_row_2), .Row_3(joysticksystem_1_row_3),
    .Row_4(joysticksystem_1_row_4), .Row_0_2(joysticksystem_1_row_0_2), .Row_1_2(joysticksystem_1_row_1_2),
    .Row_2_2(joysticksystem_1_row_2_2), .Row_3_2(joysticksystem_1_row_3_2), .Row_4_2(joysticksystem_1_row_4_2));
  SpeedSystem speedsystem_1 (
    .in_1(U_out), .in_2(D_out), .a(speedsystem_1_a), .b(speedsystem_1_b), .c(speedsystem_1_c),
    .d(speedsystem_1_d), .e(speedsystem_1_e), .f(speedsystem_1_f), .g(speedsystem_1_g));
  JoystickSystem joysticksystem_2 (
    .JoystickX(joystick_2_x), .JoystickY(joystick_2_y), .Row_0(joysticksystem_2_row_0),
    .Row_1(joysticksystem_2_row_1), .Row_2(joysticksystem_2_row_2), .Row_3(joysticksystem_2_row_3),
    .Row_4(joysticksystem_2_row_4), .Row_0_2(joysticksystem_2_row_0_2), .Row_1_2(joysticksystem_2_row_1_2),
    .Row_2_2(joysticksystem_2_row_2_2), .Row_3_2(joysticksystem_2_row_3_2), .Row_4_2(joysticksystem_2_row_4_2));
  DotMatrix #(.inputtype("row"), .matrixcols(4), .matrixrows(5)) dotmatrix_1 (
    .row0(joysticksystem_1_row_0), .row1(joysticksystem_1_row_1), .row2(joysticksystem_1_row_2),
    .row3(joysticksystem_1_row_3), .row4(joysticksystem_1_row_4));
  DotMatrix #(.inputtype("row"), .matrixcols(4), .matrixrows(5)) dotmatrix_2 (
    .row0(joysticksystem_1_row_0_2), .row1(joysticksystem_1_row_1_2), .row2(joysticksystem_1_row_2_2),
    .row3(joysticksystem_1_row_3_2), .row4(joysticksystem_1_row_4_2));
  _7_Segment_Display u_7_segment_display_1 (
    .g(speedsystem_1_g), .f(speedsystem_1_f), .a(speedsystem_1_a), .b(speedsystem_1_b), .e(speedsystem_1_e),
    .d(speedsystem_1_d), .c(speedsystem_1_c));  // open: dp
  DotMatrix #(.inputtype("row"), .matrixcols(4), .matrixrows(5)) dotmatrix_3 (
    .row0(joysticksystem_2_row_0), .row1(joysticksystem_2_row_1), .row2(joysticksystem_2_row_2),
    .row3(joysticksystem_2_row_3), .row4(joysticksystem_2_row_4));
  DotMatrix #(.inputtype("row"), .matrixcols(4), .matrixrows(5)) dotmatrix_4 (
    .row0(joysticksystem_2_row_0_2), .row1(joysticksystem_2_row_1_2), .row2(joysticksystem_2_row_2_2),
    .row3(joysticksystem_2_row_3_2), .row4(joysticksystem_2_row_4_2));
endmodule
