// Logisim project FromJoystickXToMatrix.circ as structural Verilog: 8 circuits, main circuit FirstRowX
module FirstRowX (
  input  [2:0] JoystickX,
  input  [2:0] RightDir,
  input  [2:0] LeftDir,
  input  [2:0] IdleDir,
  output [3:0] MatrixRow
);

  ThreeCaseSwitch4Bits threecaseswitch4bits_1 (
    .Value(JoystickX), .FirstCase(RightDir), .FirstValue(4'b1110), .SecondCase(LeftDir),
    .SecondValue(4'b1000), .ThirdCase(IdleDir), .ThirdValue(4'b0111), .DEFAULT(4'b1111),
    .ReturnedValue(MatrixRow));
endmodule

module SecondRowX (
  input  [2:0] JoystickX,
  input  [2:0] RightDir,
  input  [2:0] LeftDir,
  input  [2:0] IdleDir,
  output [3:0] MatrixRow
);

  ThreeCaseSwitch4Bits threecaseswitch4bits_1 (
    .Value(JoystickX), .FirstCase(RightDir), .FirstValue(4'b1001), .SecondCase(LeftDir),
    .SecondValue(4'b1000), .ThirdCase(IdleDir), .ThirdValue(4'b1000), .DEFAULT(4'b1000),
    .ReturnedValue(MatrixRow));
endmodule

module ThirdRowX (
  input  [2:0] JoystickX,
  input  [2:0] RightDir,
  input  [2:0] LeftDir,
  input  [2:0] IdleDir,
  output [3:0] MatrixRow
);

  ThreeCaseSwitch4Bits threecaseswitch4bits_1 (
    .Value(JoystickX), .FirstCase(RightDir), .FirstValue(4'b1110), .SecondCase(LeftDir),
    .SecondValue(4'b1000), .ThirdCase(IdleDir), .ThirdValue(4'b1111), .DEFAULT(4'b1111),
    .ReturnedValue(MatrixRow));
endmodule

module FourthRowX (
  input  [2:0] JoystickX,
  input  [2:0] RightDir,
  input  [2:0] LeftDir,
  input  [2:0] IdleDir,
  output [3:0] MatrixRow
);

  ThreeCaseSwitch4Bits threecaseswitch4bits_1 (
    .Value(JoystickX), .FirstCase(RightDir), .FirstValue(4'b1010), .SecondCase(LeftDir),
    .SecondValue(4'b1000), .ThirdCase(IdleDir), .ThirdValue(4'b0001), .DEFAULT(4'b1000),
    .ReturnedValue(MatrixRow));
endmodule

module FifthRowX (
  input  [2:0] JoystickX,
  input  [2:0] RightDir,
  input  [2:0] LeftDir,
  input  [2:0] IdleDir,
  output [3:0] MatrixRow
);

  ThreeCaseSwitch4Bits threecaseswitch4bits_1 (
    .Value(JoystickX), .FirstCase(RightDir), .FirstValue(4'b1001), .SecondCase(LeftDir),
    .SecondValue(4'b1111), .ThirdCase(IdleDir), .ThirdValue(4'b1110), .DEFAULT(4'b1111),
    .ReturnedValue(MatrixRow));
endmodule

module RowsZeroOne (
  input  [2:0] JoystickX,
  output [3:0] Row_0,
  output [3:0] Row_1
);

  FirstRowX firstrowx_1 (
    .JoystickX(JoystickX), .RightDir(3'b101), .LeftDir(3'b000), .IdleDir(3'b010), .MatrixRow(Row_0));
  SecondRowX secondrowx_1 (
    .JoystickX(JoystickX), .RightDir(3'b101), .LeftDir(3'b000), .IdleDir(3'b010), .MatrixRow(Row_1));
endmodule

module RowsTwoThree (
  input  [2:0] JoystickX,
  output [3:0] Row_2,
  output [3:0] Row_3
);

  ThirdRowX thirdrowx_1 (
    .JoystickX(JoystickX), .RightDir(3'b101), .LeftDir(3'b000), .IdleDir(3'b010), .MatrixRow(Row_2));
  FourthRowX fourthrowx_1 (
    .JoystickX(JoystickX), .RightDir(3'b101), .LeftDir(3'b000), .IdleDir(3'b010), .MatrixRow(Row_3));
endmodule

module FromJoystickXToMatrix (
  input  [2:0] JoystickX,
  output [3:0] Row_0,
  output [3:0] Row_1,
  output [3:0] Row_2,
  output [3:0] Row_3,
  output [3:0] Row_4
);

  RowsZeroOne rowszeroone_1 (.JoystickX(JoystickX), .Row_0(Row_0), .Row_1(Row_1));
  RowsTwoThree rowstwothree_1 (.JoystickX(JoystickX), .Row_2(Row_2), .Row_3(Row_3));
  FifthRowX fifthrowx_1 (
    .JoystickX(JoystickX), .RightDir(3'b101), .LeftDir(3'b000), .IdleDir(3'b010), .MatrixRow(Row_4));
endmodule
