// Logisim project ButtonSpeedSystem.circ as structural Verilog: 1 circuit, main circuit ButtonSpeedSystem
module ButtonSpeedSystem (
  input  in_1,
  input  in_2,
  output a,
  output b,
  output c,
  output d,
  output e,
  output f,
  output g
);

  wire clock_1_out;
  wire [2:0] buttonspeed_1_s0, register_1_q;

  Clock clock_1 (.out(clock_1_out));
  Register #(.width(3)) register_1 (.D(buttonspeed_1_s0), .Q(register_1_q), .clk(clock_1_out));  // open: en, clr
  ButtonSpeed buttonspeed_1 (
    .D2(register_1_q[2]), .D1(register_1_q[1]), .D0(register_1_q[0]), .U(in_1), .D(in_2),
    .S2(buttonspeed_1_s0[2]), .S1(buttonspeed_1_s0[1]), .S0(buttonspeed_1_s0[0]));
  SevenSegmentRepresentation sevensegmentrepresentation_1 (
    .Number(buttonspeed_1_s0), ._7SegmentNumber({g, f, e, d, c, b, a}));
endmodule
