// Logisim project SpeedSystem.circ as structural Verilog: 1 circuit, main circuit SpeedSystem
module SpeedSystem (
  input  in_1,
  input  in_2,
  output a,
  output b,
  output c,
  output d,
  output e,
  output f,
  output g
);

  wire [2:0] buttonspeedsystem_1_speed;

  ButtonSpeedSystem buttonspeedsystem_1 (.U(in_1), .D(in_2), .Speed(buttonspeedsystem_1_speed));
  SevenSegmentRepresentation sevensegmentrepresentation_1 (
    .Number(buttonspeedsystem_1_speed), ._7SegmentNumber({g, f, e, d, c, b, a}));
endmodule
