// Logisim project SumAdjuster.circ as structural Verilog: 1 circuit, main circuit SumAdjuster
module SumAdjuster (
  input  [3:0] Sum,
  output [3:0] Sum_2
);

  wire equality4bits_1_eqab, equality4bits_2_eqab;
  wire [3:0] multiplexer_2_out;

  Equality4Bits equality4bits_1 (.A(Sum), .B(4'b1111), .EQAB(equality4bits_1_eqab));
  Equality4Bits equality4bits_2 (.A(Sum), .B(4'b1000), .EQAB(equality4bits_2_eqab));
  Multiplexer #(.width(4)) multiplexer_1 (
    .in0(multiplexer_2_out), .in1(4'b0000), .out(Sum_2), .sel(equality4bits_1_eqab));  // open: en
  Multiplexer #(.width(4)) multiplexer_2 (
    .in0(Sum), .in1(4'b0111), .out(multiplexer_2_out), .sel(equality4bits_2_eqab));  // open: en

  // Notes on the sheet:
  //   MinSpeed
  //   MaxSpeed
endmodule
