// Logisim project Switch.circ as structural Verilog: 2 circuits, main circuit SwitchThreeCase7Bit
module SwitchThreeCase7Bit (
  input  [2:0] Value,
  input  [2:0] FirstCase,
  input  [6:0] FirstValue,
  input  [2:0] SecondCase,
  input  [6:0] SecondValue,
  input  [2:0] ThirdCase,
  input  [6:0] ThirdValue,
  input  [6:0] DEFAULT,
  output [6:0] ReturnedValue
);

  wire equality3bits_1_aqab, equality3bits_2_aqab, equality3bits_3_aqab;
  wire [6:0] multiplexer_2_out, multiplexer_3_out;

  Equality3Bits equality3bits_1 (.A(Value), .B(FirstCase), .AQAB(equality3bits_1_aqab));
  Equality3Bits equality3bits_2 (.A(Value), .B(SecondCase), .AQAB(equality3bits_2_aqab));
  Equality3Bits equality3bits_3 (.A(Value), .B(ThirdCase), .AQAB(equality3bits_3_aqab));
  Multiplexer #(.width(7)) multiplexer_1 (
    .in0(multiplexer_2_out), .in1(FirstValue), .out(ReturnedValue), .sel(equality3bits_1_aqab));  // open: en
  Multiplexer #(.width(7)) multiplexer_2 (
    .in0(multiplexer_3_out), .in1(SecondValue), .out(multiplexer_2_out), .sel(equality3bits_2_aqab));  // open: en
  Multiplexer #(.width(7)) multiplexer_3 (
    .in0(DEFAULT), .in1(ThirdValue), .out(multiplexer_3_out), .sel(equality3bits_3_aqab));  // open: en
endmodule

module SwitchOneCase7Bits (
  input  [2:0] Value,
  input  [2:0] FirstCase,
  input  [6:0] FirstValue,
  input  [6:0] Default,
  output [6:0] ReturnedValue
);

  wire equality3bits_1_aqab;

  Equality3Bits equality3bits_1 (.A(Value), .B(FirstCase), .AQAB(equality3bits_1_aqab));
  Multiplexer #(.width(7)) multiplexer_1 (
    .in0(Default), .in1(FirstValue), .out(ReturnedValue), .sel(equality3bits_1_aqab));  // open: en
endmodule
